# Fritzing sketch schematic (saved by Fritzing 0.9.6b)

parts:
  J1 = DHT11 basic temperature-humidity sensor [form="♂ (male)" package=THT]
  U1 = ESP8266 NodeMCU LoLin module
  Mod1 = KY-019 5V Relay Module [package="Breakout board"]

nets:
  VCC: J1.VCC, U1.3V3
  N1: J1.OUT, U1.D2
  GND: J1.GND, U1.GND, Mod1.-
  N2: U1.D1, Mod1.S
  N3: U1.Vin, Mod1.+

custom parts:
  DHT11 basic temperature-humidity sensor: The DHT11 is a basic, ultra low-cost digital temperature and humidity sensor. It uses a capacitive humidity sensor and a thermistor to measure the surrounding air, and spits out a digital signal on the data pin (no analog input pins needed). Its fairly simple to use, but requires careful timing to grab data. The only real downside of this sensor is you can only get new data from it once every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
  ESP8266 NodeMCU LoLin module: ESP8266 based NodeMCU
  KY-019 5V Relay Module: KY-019 5V Relay module, used to control AC circuits.
